# Fritzing sketch magnet-sensor (saved by Fritzing 0.9.3b)
breadboards: 1

parts:
  U1 = NodeMCU V1.0
  S1 = Magnetic Door Switch [package=reed_switch_plastic]
  R1 = Resistor [tolerance=±5% resistance=220 package="0805 [SMD]"]

nets:
  N1: U1.D1, S1.2, R1.Pin_0
  N2: U1.3V3, S1.1
  N3: U1.GND, R1.Pin_1

custom parts:
  NodeMCU V1.0: ESP8266 based NodeMCU
